# Fritzing sketch LED_Driver_USB_To_WS2812 (saved by Fritzing 0.9.3b)

parts:
  U1 = ESP8266 NodeMCU LoLin module
  IC1 = Voltage Regulator [package=to-220-alt]
  C1 = Electrolytic Capacitor [capacitance=100µF package="200 mil [THT, electrolytic]"]
  R1 = Resistor [tolerance=±5% resistance=220 package="0402 [SMD]"]
  CONN1 = USB connector [package=THT]
  S1 = Pushbutton [package="[THT]"]
  U2 = WS2812 RGB LED strip

nets:
  N1: U1.D7, R1.Pin_1
  N2: U1.Vin, IC1.OUT
  N3: IC1.IN, C1.+, S1.Pin_2
  N4: C1.-, CONN1.chassis5, U2.GND
  N5: R1.Pin_0, U2.DIN
  N6: CONN1.5V, S1.Pin_4

notes:
  USB 2.1A, 5V
  1000uF
  TO-220
  WS281x (120x)
  330Ω

custom parts:
  ESP8266 NodeMCU LoLin module: ESP8266 based NodeMCU
  WS2812 RGB LED strip: WS2812 strip
