# Fritzing sketch LED_Driver_USB_To_WS2812_MOSFET_Switch (saved by Fritzing 0.9.3b)

parts:
  U1 = ESP8266 NodeMCU LoLin module
  C1 = Electrolytic Capacitor [capacitance=100µF package="200 mil [THT, electrolytic]"]
  CONN1 = USB connector [package=THT]
  U2 = WS2812 RGB LED strip
  U3 = SPDT Slide Switch [package=ayz0202]
  Part1 = Logic Level Converter
  R1 = Resistor [tolerance=±5% resistance=470 package="2512 [SMD]"]
  Q1 = Basic FET P-Channel [package="TO220 [THT]"]  # not connected
  R2 = Resistor [tolerance=±5% resistance=220 package="2512 [SMD]"]
  R3 = Resistor [tolerance=±5% resistance=100k package="2512 [SMD]"]

nets:
  N1: U1.D4, R2.Pin_0
  N2: U1.D7, Part1.RX2_LV
  N3: U1.3V3, Part1.LV
  N4: U1.Vin, U3.2
  GND: C1.-, CONN1.GND, CONN1.chassis5, CONN1.chassis6, U2.GND
  N5: C1.+, U2.VCC
  N6: CONN1.5V, U3.3
  N7: U2.DIN, R1.Pin_0
  N8: Part1.TX2_HV, R1.Pin_1
  N9: R2.Pin_1, R3.Pin_1

notes:
  USB 2.1A, 5V
  1000uF
  WS281x (120x)
  470Ω
  Iteration 0
  WS2812
  NodeMCU
  30 LEDs
  Single Power Source
  Toggle (Power)
  Logic Level Cnv
  220Ω
  100kΩ
  fqp27p06

custom parts:
  ESP8266 NodeMCU LoLin module: ESP8266 based NodeMCU
  WS2812 RGB LED strip: WS2812 strip
