# Fritzing sketch LED_Driver_USB_To_WS2812_Single_Power (saved by Fritzing 0.9.3b)

parts:
  U1 = ESP8266 NodeMCU LoLin module
  C1 = Electrolytic Capacitor [capacitance=100µF package="200 mil [THT, electrolytic]"]
  CONN1 = USB connector [package=THT]
  U2 = WS2812 RGB LED strip
  U3 = SPDT Slide Switch [package=ayz0202]
  Part1 = Logic Level Converter
  R1 = Resistor [tolerance=±5% resistance=220 package="2512 [SMD]"]

nets:
  N1: U1.D7, Part1.RX2_LV
  N2: U1.3V3, Part1.LV
  VIN: U1.Vin, C1.+, CONN1.5V, U3.3, U3.2
  N3: C1.-, CONN1.chassis5, U2.GND
  N4: U2.DIN, R1.Pin_0
  N5: Part1.TX2_HV, R1.Pin_1

notes:
  USB 2.1A, 5V
  1000uF
  WS281x (120x)
  470Ω
  Iteration 0
  WS2812
  NodeMCU
  30 LEDs
  Single Power Source
  Toggle (Power)
  Logic Level Cnv

custom parts:
  ESP8266 NodeMCU LoLin module: ESP8266 based NodeMCU
  WS2812 RGB LED strip: WS2812 strip
